# Fritzing sketch Sketch (saved by Fritzing 0.8.3b)

parts:
  Parte1 = Arduino Uno (Rev3)
  J1 = Infrared Proximity Sensor

nets:
  GND: Parte1.GND, J1.GND
  N1: Parte1.D5_PWM, J1.Vout
  5V: Parte1.5V, J1.Vcc
